// Logisim project pk16.circ as structural Verilog: 17 circuits, main circuit main
module main (
  input  [15:0] in_1
);

  wire clock_1_out, counter_1_carry, pull_resistor_1_node, pull_resistor_2_node, pull_resistor_3_node,
       pull_resistor_4_node;
  wire [3:0] bus_encoder_1_opcode_format;
  wire [7:0] bus_encoder_1_destination_register, bus_encoder_1_source_register, rom_chip_1_io;
  wire [14:0] counter_1_q;
  wire [15:0] main_register_1_read_1, main_register_1_read_2, opcode_decoder_1_instruction;

  Clock clock_1 (.out(clock_1_out));
  Counter #(.max('h7fff), .width(15)) counter_1 (
    .clr(pull_resistor_1_node), .load(pull_resistor_1_node), .up(1'b1), .count(1'b1), .clk(clock_1_out),
    .carry(counter_1_carry), .Q(counter_1_q));  // open: D
  Pull_Resistor pull_resistor_1 (.node(pull_resistor_1_node));
  Pull_Resistor pull_resistor_2 (.node(pull_resistor_2_node));
  Pull_Resistor #(.pull(1)) pull_resistor_3 (.node(pull_resistor_3_node));
  rom_chip rom_chip_1 (
    .address(counter_1_q), .cs(pull_resistor_2_node), .oe(pull_resistor_2_node), .we(pull_resistor_3_node),
    .io(rom_chip_1_io));
  opcode_decoder opcode_decoder_1 (
    .read_inst(rom_chip_1_io), .instruction(opcode_decoder_1_instruction));  // open: inst_complete, read_program
  bus_encoder bus_encoder_1 (
    .instruction(opcode_decoder_1_instruction), .opcode_format(bus_encoder_1_opcode_format),
    .destination_register(bus_encoder_1_destination_register), .source_register(bus_encoder_1_source_register));
  Pull_Resistor pull_resistor_4 (.node(pull_resistor_4_node));
  main_register main_register_1 (
    .clock(clock_1_out), .not_select_1(bus_encoder_1_destination_register[0]),
    .not_select_2(bus_encoder_1_source_register[0]), .write_value(in_1),
    .disable_upper(pull_resistor_4_node), .disable_lower(pull_resistor_4_node),
    .read_1(main_register_1_read_1), .read_2(main_register_1_read_2));
  main_register main_register_2 (
    .clock(clock_1_out), .not_select_1(bus_encoder_1_destination_register[1]),
    .not_select_2(bus_encoder_1_source_register[1]), .write_value(in_1),
    .disable_upper(pull_resistor_4_node), .disable_lower(pull_resistor_4_node),
    .read_1(main_register_1_read_1), .read_2(main_register_1_read_2));
endmodule

module opcode_decoder (
  input  [7:0] read_inst,
  input  inst_complete,
  output [15:0] instruction,
  output read_program
);

  wire clock_1_out, n7402_1_pin4, n7402_1_pin10, n7402_1_pin11, n7402_1_pin13, n7474_1_pin2, n7474_1_pin5;

  _7402 u_7402_1 (
    .pin4(n7402_1_pin4), .pin5(inst_complete), .pin6(inst_complete), .pin13(n7402_1_pin13),
    .pin12(read_program), .pin11(n7402_1_pin11), .pin10(n7402_1_pin10), .pin9(n7402_1_pin13),
    .pin8(n7402_1_pin13));  // open: pin1, pin2, pin3
  Clock clock_1 (.out(clock_1_out));
  _7474 u_7474_1 (
    .pin1(n7402_1_pin4), .pin2(n7474_1_pin2), .pin3(clock_1_out), .pin5(n7474_1_pin5), .pin6(n7402_1_pin11),
    .pin13(n7402_1_pin4), .pin12(n7474_1_pin5), .pin11(clock_1_out), .pin9(read_program));  // open: pin4, pin10, pin8
  register_8 opcode_register_lower (
    .data(read_inst), .clken(n7474_1_pin5), .clk(clock_1_out), .out_4(instruction[15:8]));
  register_8 opcode_register_upper (
    .data(read_inst), .clken(n7402_1_pin10), .clk(clock_1_out), .out_4(instruction[7:0]));
  // also tied to VCC on the sheet: n7474_1_pin2
endmodule

module main_register (
  input  clock,
  input  not_select_1,
  input  not_select_2,
  input  [15:0] write_value,
  input  disable_upper,
  input  disable_lower,
  output [15:0] read_1,
  output [15:0] read_2
);

  wire n7414_1_pin2, n7414_1_pin12, n7432_1_pin3, n7432_1_pin6;
  wire [7:0] register_8_1_out_4, register_8_2_out_4;

  _7432 u_7432_1 (
    .pin1(not_select_1), .pin2(disable_upper), .pin3(n7432_1_pin3), .pin4(not_select_1),
    .pin5(disable_lower), .pin6(n7432_1_pin6));  // open: pin13, pin12, pin11, pin10, pin9, pin8
  _7414 u_7414_1 (
    .pin1(not_select_2), .pin2(n7414_1_pin2), .pin13(not_select_1), .pin12(n7414_1_pin12));  // open: pin3, pin4, pin5, pin6, pin11, pin10, pin9, pin8
  register_8 register_8_1 (.data(write_value[7:0]), .clken(n7432_1_pin6), .clk(clock), .out_4(register_8_1_out_4));
  register_8 register_8_2 (.data(write_value[15:8]), .clken(n7432_1_pin3), .clk(clock), .out_4(register_8_2_out_4));
  switch_16 switch_16_1 (.a({register_8_2_out_4, register_8_1_out_4}), .switch(n7414_1_pin12), .switched(read_1));
  switch_16 switch_16_2 (.a({register_8_2_out_4, register_8_1_out_4}), .switch(n7414_1_pin2), .switched(read_2));
endmodule

module alu (
  input  [15:0] a,
  input  [15:0] b,
  input  in_3,
  input  cin,
  output [15:0] o,
  output cout
);

  wire [15:0] mux_16_1_o, negate_16_1_inverted;

  negate_16 negate_16_1 (.invert(b), .inverted(negate_16_1_inverted));
  mux_16 mux_16_1 (.a(b), .b(negate_16_1_inverted), .ab(in_3), .o(mux_16_1_o));  // open: e
  adder_16 adder_16_1 (.a(a), .b(mux_16_1_o), .cin(cin), .sum(o), .cout(cout));
endmodule

module adder_16 (
  input  [15:0] a,
  input  [15:0] b,
  input  cin,
  output [15:0] sum,
  output cout
);

  wire adder_8_1_cout;

  adder_8 adder_8_1 (.a(a[7:0]), .b(b[7:0]), .cin(cin), .sum(sum[7:0]), .cout(adder_8_1_cout));
  adder_8 adder_8_2 (.a(a[15:8]), .b(b[15:8]), .cin(adder_8_1_cout), .sum(sum[15:8]), .cout(cout));
endmodule

module adder_8 (
  input  [7:0] a,
  input  [7:0] b,
  input  cin,
  output [7:0] sum,
  output cout
);

  wire n74283_1_pin7;

  _74283 u_74283_1 (
    .pin1(sum[5]), .pin2(b[5]), .pin3(a[5]), .pin4(sum[4]), .pin5(a[4]), .pin6(b[4]), .pin7(n74283_1_pin7),
    .pin15(b[6]), .pin14(a[6]), .pin13(sum[6]), .pin12(a[7]), .pin11(b[7]), .pin10(sum[7]), .pin9(cout));
  _74283 u_74283_2 (
    .pin1(sum[1]), .pin2(b[1]), .pin3(a[1]), .pin4(sum[0]), .pin5(a[0]), .pin6(b[0]), .pin7(cin),
    .pin15(b[2]), .pin14(a[2]), .pin13(sum[2]), .pin12(a[3]), .pin11(b[3]), .pin10(sum[3]),
    .pin9(n74283_1_pin7));
endmodule

module negate_16 (
  input  [15:0] invert,
  output [15:0] inverted
);

  wire adder_16_1_cout;
  wire [15:0] n7414_1_pin12;

  _7414 u_7414_1 (
    .pin1(invert[5]), .pin2(n7414_1_pin12[5]), .pin3(invert[4]), .pin4(n7414_1_pin12[4]), .pin5(invert[3]),
    .pin6(n7414_1_pin12[3]), .pin13(invert[0]), .pin12(n7414_1_pin12[0]), .pin11(invert[1]),
    .pin10(n7414_1_pin12[1]), .pin9(invert[2]), .pin8(n7414_1_pin12[2]));
  _7414 u_7414_2 (
    .pin1(invert[11]), .pin2(n7414_1_pin12[11]), .pin3(invert[10]), .pin4(n7414_1_pin12[10]),
    .pin5(invert[9]), .pin6(n7414_1_pin12[9]), .pin13(invert[6]), .pin12(n7414_1_pin12[6]),
    .pin11(invert[7]), .pin10(n7414_1_pin12[7]), .pin9(invert[8]), .pin8(n7414_1_pin12[8]));
  _7414 u_7414_3 (
    .pin5(invert[15]), .pin6(n7414_1_pin12[15]), .pin13(invert[12]), .pin12(n7414_1_pin12[12]),
    .pin11(invert[13]), .pin10(n7414_1_pin12[13]), .pin9(invert[14]), .pin8(n7414_1_pin12[14]));  // open: pin1, pin2, pin3, pin4
  adder_16 adder_16_1 (.a({16{1'b0}}), .b(n7414_1_pin12), .cin(1'b1), .sum(inverted), .cout(adder_16_1_cout));
endmodule

module subber_4 (
  input  [3:0] a,
  input  cin,
  input  [3:0] b,
  output cout,
  output [3:0] sum
);

  wire n7414_1_pin10, n7414_1_pin11, n7414_1_pin12, n7414_1_pin13, n74283_1_pin2, n74283_1_pin6,
       n74283_1_pin11, n74283_1_pin15;

  _74283 u_74283_1 (
    .pin1(sum[1]), .pin2(n74283_1_pin2), .pin3(a[1]), .pin4(sum[0]), .pin5(a[0]), .pin6(n74283_1_pin6),
    .pin7(cin), .pin15(n74283_1_pin15), .pin14(a[2]), .pin13(sum[2]), .pin12(a[3]), .pin11(n74283_1_pin11),
    .pin10(sum[3]), .pin9(cout));
  _7414 u_7414_1 (
    .pin1(b[3]), .pin2(n74283_1_pin11), .pin3(b[2]), .pin4(n74283_1_pin15), .pin5(b[1]),
    .pin6(n74283_1_pin2), .pin13(n7414_1_pin13), .pin12(n7414_1_pin12), .pin11(n7414_1_pin11),
    .pin10(n7414_1_pin10), .pin9(b[0]), .pin8(n74283_1_pin6));
  Pull_Resistor pull_resistor_1 (.node(n7414_1_pin12));
  Pull_Resistor pull_resistor_2 (.node(n7414_1_pin10));
  Pull_Resistor #(.pull(1)) pull_resistor_3 (.node(n7414_1_pin13));
  Pull_Resistor #(.pull(1)) pull_resistor_4 (.node(n7414_1_pin11));
endmodule

module mux_4 (
  input  in_1,
  input  ab,
  input  [3:0] a,
  output [3:0] out_4
);

  wire dip_74157_1_p1, pull_resistor_1_node;

  Pull_Resistor pull_resistor_1 (.node(pull_resistor_1_node));
  // DIP_74157 dip_74157_1: pin names not known; wires that end beside it: dip_74157_1_p1, out_4[2], in_1, a[2], out_4[3], dip_74157_1_p1, a[3], pull_resistor_1_node, out_4[1], a[1], out_4[0], a[0], ab
endmodule

module mux_16 (
  input  [15:0] a,
  input  [15:0] b,
  input  ab,
  input  e,
  output [15:0] o
);

  wire not_1_out;

  not not_1 (not_1_out, e);
  Multiplexer #(.enable("true"), .width(16)) multiplexer_1 (.in0(a), .in1(b), .out(o), .sel(ab), .en(not_1_out));
endmodule

module switch_4 (
  input  [3:0] a,
  input  switch,
  output [3:0] switched
);

  _7408 u_7408_1 (
    .pin1(a[2]), .pin2(switch), .pin3(switched[2]), .pin4(a[3]), .pin5(switch), .pin6(switched[3]),
    .pin13(a[1]), .pin12(switch), .pin11(switched[1]), .pin10(a[0]), .pin9(switch), .pin8(switched[0]));
endmodule

module switch_8 (
  input  [7:0] value,
  input  switch,
  output [7:0] out_3
);

  switch_4 switch_4_1 (.a(value[3:0]), .switch(switch), .switched(out_3[3:0]));
  switch_4 switch_4_2 (.a(value[7:4]), .switch(switch), .switched(out_3[7:4]));
endmodule

module switch_16 (
  input  [15:0] a,
  input  switch,
  output [15:0] switched
);

  switch_4 switch_4_1 (.a(a[3:0]), .switch(switch), .switched(switched[3:0]));
  switch_4 switch_4_2 (.a(a[7:4]), .switch(switch), .switched(switched[7:4]));
  switch_4 switch_4_3 (.a(a[11:8]), .switch(switch), .switched(switched[11:8]));
  switch_4 switch_4_4 (.a(a[15:12]), .switch(switch), .switched(switched[15:12]));
endmodule

module register_8 (
  input  [7:0] data,
  input  clken,
  input  clk,
  output [7:0] out_4
);

  _74377 u_74377_1 (
    .pin1(clken), .pin2(out_4[0]), .pin3(data[0]), .pin4(data[1]), .pin5(out_4[1]), .pin6(out_4[2]),
    .pin7(data[2]), .pin8(data[3]), .pin9(out_4[3]), .pin19(out_4[7]), .pin18(data[7]), .pin17(data[6]),
    .pin16(out_4[6]), .pin15(out_4[5]), .pin14(data[5]), .pin13(data[4]), .pin12(out_4[4]), .pin11(clk));
endmodule

module rom_chip (
  input  [14:0] address,
  input  cs,
  input  oe,
  input  we,
  output [7:0] io
);

  wire and_1_out, not_1_out, not_2_out;
  wire [7:0] rom_1_data;

  ROM #(.addrWidth(15)) rom_1 (.addr(address), .data(rom_1_data));
  assign io = and_1_out ? rom_1_data : 8'bz;  // Controlled_Buffer controlled_buffer_1
  not not_1 (not_1_out, cs);
  not not_2 (not_2_out, oe);
  and and_1 (and_1_out, not_1_out, not_2_out, we);

  // Notes on the sheet:
  //   contents of rom_1 (hex, n*v repeats v):
  //   d0 2 40 4 8*ff d e f
endmodule

module bus_encoder (
  input  [15:0] instruction,
  output [3:0] opcode_format,
  output [7:0] destination_register,
  output [7:0] source_register
);

  wire [2:0] bit_extender_1_out;
  wire [7:4] bit_decoder_3_1_decoded;

  assign bit_extender_1_out = {{1{1'b0}}, instruction[15:14]};  // Bit_Extender bit_extender_1
  bit_decoder_3 bit_decoder_3_1 (.in_1(bit_extender_1_out), .decoded({bit_decoder_3_1_decoded, opcode_format}));
  bit_decoder_3 bit_decoder_3_2 (.in_1(instruction[10:8]), .decoded(destination_register));
  bit_decoder_3 bit_decoder_3_3 (.in_1(instruction[13:11]), .decoded(source_register));
endmodule

module bit_decoder_3 (
  input  [2:0] in_1,
  output [7:0] decoded
);

  // DIP_74138 dip_74138_1: pin names not known; wires that end beside it: in_1[0], in_1[1], in_1[2], 1'b0, 1'b0, 1'b1, decoded[7], decoded[0], decoded[1], decoded[2], decoded[3], decoded[4], decoded[5], decoded[6]
endmodule
